// Logisim project problem1_logisim.circ as structural Verilog
module main (
  input  a,
  input  b,
  input  c,
  input  d,
  output output1,
  output output2
);

  problem1 u1 (.a(a), .b(b), .c(c), .d(d), .out1(output1), .out2(output2));
endmodule

// VHDL entity problem1, as the project stores it:
library ieee;
use ieee.std_logic_1164.all;

entity problem1 is
    port (
        a, b, c, d : in  std_logic;
        out1, out2 : out std_logic
    );
end problem1;

architecture dataflow of problem1 is
begin
    out1 <= a and b and c and d;
    out2 <= a or b or c or d;
end dataflow;
