// Logisim project problem3_logisim.circ as structural Verilog
module main (
  input  en,
  input  [3:0] dat
);

  wire [7:0] problem3_1_display;

  _7_Segment_Display u_7_segment_display_1 (
    .g(problem3_1_display[1]), .f(problem3_1_display[2]), .a(problem3_1_display[7]),
    .b(problem3_1_display[6]), .e(problem3_1_display[3]), .d(problem3_1_display[4]),
    .c(problem3_1_display[5]), .dp(problem3_1_display[0]));
  problem3 problem3_1 (.en(en), .dat(dat), .display(problem3_1_display));
endmodule

// VHDL entity problem3, as the project stores it:
library ieee;
use ieee.std_logic_1164.all;

entity problem3 is
    port (
        en      : in  std_logic;
        dat     : in  std_logic_vector(3 downto 0);
        display : out std_logic_vector(7 downto 0)
    );
end problem3;

architecture bhv of problem3 is
begin
    process(en, dat)
    begin
        if en = '0' then
            display <= "ZZZZZZZZ";
        else
            case dat is
                when "0000" => display <= "11101110"; -- a
                when "0001" => display <= "00111110"; -- b
                when "0010" => display <= "00011010"; -- c
                when "0011" => display <= "01111010"; -- d
                when "0100" => display <= "10001110"; -- f
                when "0101" => display <= "11110110"; -- g
                when others => display <= "00000000";
            end case;
        end if;
    end process;
end bhv;
