// Logisim project problem4_logisim.circ as structural Verilog
module main (
  input  in_1,
  input  in_2,
  input  in_3,
  input  in_4,
  input  in_5,
  input  in_6,
  input  in_7,
  input  in_8,
  input  in_9,
  input  in_10,
  input  in_11,
  input  in_12,
  input  in_13,
  input  in_14,
  input  in_15,
  input  in_16,
  input  in_17,
  input  in_18,
  input  in_19,
  input  in_20,
  input  in_21,
  input  in_22,
  input  in_23,
  input  in_24,
  input  in_25,
  output result
);

  problem4 problem4_1 (
    .vt({in_1, in_2, in_3, in_4, in_5, in_6, in_7, in_8, in_9, in_10, in_11, in_12, in_13, in_14, in_15, in_16, in_17, in_18, in_19, in_20, in_21, in_22, in_23, in_24, in_25}),
    .result(result));
endmodule

// VHDL entity problem4, as the project stores it:
library ieee;
use ieee.std_logic_1164.all;

entity problem4 is
    port (
        vt     : in  std_logic_vector(25 downto 1);
        result : out std_logic
    );
end problem4;

architecture bhv of problem4 is
begin
    process(vt)
        variable sum : integer range 0 to 25;
    begin
        sum := 0;

        for i in 1 to 25 loop
            if vt(i) = '1' then
                sum := sum + 1;
            end if;
        end loop;

        if sum >= 13 then
            result <= '1';
        else
            result <= '0';
        end if;
    end process;
end bhv;
